// Logisim project cache_brams.circ as structural Verilog: 1 circuit, main circuit main
module main (
  input  [15:0] activacion,
  input  [20:0] address,
  input  L_E_prime,
  input  request,
  input  reset,
  input  clk,
  output valido,
  output error,
  output [15:0] salida
);

  wire and_1_out, and_2_out, and_3_out, and_4_out, and_5_out, and_6_out, and_7_out, and_8_out, and_9_out,
       and_10_out, and_11_out, and_12_out, and_13_out, and_14_out, and_15_out, and_17_out, and_18_out,
       and_19_out, and_20_out, and_21_out, aun_vias_libres, clear_ram, comparator_1_eq, comparator_2_eq,
       comparator_3_eq, comparator_4_eq, comparator_5_eq, enable_direccion, enable_direccion_valid, enable_r,
       enable_r_valid, enable_salida_ram, enable_w, enable_w_valid, enable_w_viaX, hit_via0, hit_via1,
       hit_via2, hit_via3, hit_via4, L_E_ram, L_E_ram_valid, not_1_out, not_2_out, not_3_out, not_4_out,
       not_5_out, not_6_out, not_7_out, not_8_out, not_9_out, not_10_out, not_11_out, not_12_out, not_13_out,
       not_14_out, ocupada_via0, ocupada_via1, ocupada_via2, ocupada_via3, ocupada_via4, or_1_out, or_2_out,
       w_via0, w_via1, w_via2, w_via3, w_via4;
  wire [2:0] estado, priority_encoder_1_out, register_15_q, via_a_escribir;
  wire [4:0] multiplexer_4_out, ram_5_data;
  wire [7:0] multiplexer_1_out, multiplexer_5_out, register_17_q, register_18_q, set_bueno, set_bueno_valid,
       set_escribir, set_escribir_valid;
  wire [12:0] ram_1_data, ram_3_data, ram_6_data, ram_8_data, ram_10_data, register_1_q, register_3_q,
       register_5_q, register_8_q, register_11_q, register_14_q;
  wire [15:0] multiplexer_3_out, multiplexer_7_out, multiplexer_10_out, multiplexer_12_out,
       multiplexer_14_out, ram_2_data, ram_4_data, ram_7_data, ram_9_data, ram_11_data, register_2_q,
       register_4_q, register_6_q, register_9_q, register_12_q, register_13_q;

  Register #(.width(13)) register_1 (.D(address[20:8]), .Q(register_1_q), .clk(clk));  // open: en, clr
  and and_1 (and_1_out, w_via0, and_21_out);
  Comparator #(.width(13)) comparator_1 (.a(register_3_q), .b(address[20:8]), .eq(comparator_1_eq));  // open: gt, lt
  and and_2 (and_2_out, w_via0, and_19_out);
  not not_1 (not_1_out, estado[1]);
  and and_3 (and_3_out, estado[0], not_1_out, estado[2]);
  not not_2 (not_2_out, and_3_out);
  not not_3 (not_3_out, L_E_prime);
  Multiplexer #(.width(8), .enable("false")) multiplexer_1 (
    .in0(set_bueno), .in1(set_escribir), .out(multiplexer_1_out), .sel(enable_w));
  RAM #(.dataWidth(13), .bus("separate")) ram_1 (
    .addr(multiplexer_1_out), .din(register_1_q), .data(ram_1_data), .str(clk), .clk(and_1_out),
    .ld(L_E_ram), .clr(clear_ram));  // open: sel
  and and_4 (and_4_out, comparator_1_eq, ocupada_via0);
  Register #(.width(16)) register_2 (.D(activacion), .Q(register_2_q), .clk(clk));  // open: en, clr
  RAM #(.dataWidth(16), .bus("separate")) ram_2 (
    .addr(multiplexer_1_out), .din(register_2_q), .data(ram_2_data), .str(clk), .clk(and_2_out),
    .ld(L_E_ram), .clr(clear_ram));  // open: sel
  and and_5 (and_5_out, not_2_out, not_3_out);
  // Probe on multiplexer_1_out
  Register #(.width(13)) register_3 (.D(ram_1_data), .Q(register_3_q), .clk(clk));  // open: en, clr
  Multiplexer #(.enable("false")) multiplexer_2 (.in0(1'b1), .in1(and_4_out), .out(hit_via0), .sel(enable_salida_ram));
  Multiplexer #(.width(16), .enable("false")) multiplexer_3 (
    .in0({16{1'b0}}), .in1(register_4_q), .out(multiplexer_3_out), .sel(enable_salida_ram));
  Register #(.width(16)) register_4 (.D(ram_2_data), .Q(register_4_q), .clk(clk));  // open: en, clr
  Priority_Encoder priority_encoder_1 (
    .in0(reset), .in1(and_5_out), .in2(hit_via4), .in3(hit_via3), .in4(hit_via2), .in5(hit_via1),
    .in6(hit_via0), .out(priority_encoder_1_out));  // open: in7, en_in, gs, en_out
  Multiplexer #(.select(3), .width(5)) multiplexer_4 (
    .in0({5{1'b1}}), .in1(5'b01111), .in2(5'b00111), .in3(5'b00011), .in4(5'b00001), .out(multiplexer_4_out),
    .sel(via_a_escribir), .en(enable_w_viaX));  // open: in5, in6, in7
  // Probe on multiplexer_4_out
  and and_6 (and_6_out, w_via1, and_21_out);
  Comparator #(.width(13)) comparator_2 (.a(register_5_q), .b(address[20:8]), .eq(comparator_2_eq));  // open: gt, lt
  and and_7 (and_7_out, w_via1, and_19_out);
  // Probe on multiplexer_5_out
  RAM #(.dataWidth(13), .bus("separate")) ram_3 (
    .addr(multiplexer_1_out), .din(register_1_q), .data(ram_3_data), .str(clk), .clk(and_6_out),
    .ld(L_E_ram), .clr(clear_ram));  // open: sel
  and and_8 (and_8_out, comparator_2_eq, ocupada_via1);
  RAM #(.dataWidth(16), .bus("separate")) ram_4 (
    .addr(multiplexer_1_out), .din(register_2_q), .data(ram_4_data), .str(clk), .clk(and_7_out),
    .ld(L_E_ram), .clr(clear_ram));  // open: sel
  // Probe on salida
  Multiplexer #(.width(8), .enable("false")) multiplexer_5 (
    .in0(set_bueno_valid), .in1(set_escribir_valid), .out(multiplexer_5_out), .sel(enable_w_valid));
  Register #(.width(13)) register_5 (.D(ram_3_data), .Q(register_5_q), .clk(clk));  // open: en, clr
  Multiplexer #(.enable("false")) multiplexer_6 (.in0(1'b0), .in1(and_8_out), .out(hit_via1), .sel(enable_salida_ram));
  Multiplexer #(.width(16), .enable("false")) multiplexer_7 (
    .in0({16{1'b0}}), .in1(register_6_q), .out(multiplexer_7_out), .sel(enable_salida_ram));
  Register #(.width(16)) register_6 (.D(ram_4_data), .Q(register_6_q), .clk(clk));  // open: en, clr
  Multiplexer #(.select(3), .width(16)) multiplexer_8 (
    .in0({16{1'b1}}), .in1(16'hfffe), .in2(multiplexer_14_out), .in3(multiplexer_12_out),
    .in4(multiplexer_10_out), .in5(multiplexer_7_out), .in6(multiplexer_3_out), .out(salida),
    .sel(priority_encoder_1_out));  // open: in7, en
  and and_9 (and_9_out, clk, aun_vias_libres, enable_w_valid);
  and and_10 (and_10_out, w_via2, and_21_out);
  Comparator #(.width(13)) comparator_3 (.a(register_8_q), .b(address[20:8]), .eq(comparator_3_eq));  // open: gt, lt
  and and_11 (and_11_out, and_19_out, w_via2);
  Register #(.width(5)) register_7 (
    .D(ram_5_data), .Q({ocupada_via4, ocupada_via3, ocupada_via2, ocupada_via1, ocupada_via0}), .clk(clk));  // open: en, clr
  RAM #(.dataWidth(5), .bus("separate")) ram_5 (
    .addr(multiplexer_5_out), .din(multiplexer_4_out), .data(ram_5_data), .str(clk), .clk(and_9_out),
    .ld(L_E_ram_valid), .clr(clear_ram));  // open: sel
  RAM #(.dataWidth(13), .bus("separate")) ram_6 (
    .addr(multiplexer_1_out), .din(register_1_q), .data(ram_6_data), .str(clk), .clk(and_10_out),
    .ld(L_E_ram), .clr(clear_ram));  // open: sel
  and and_12 (and_12_out, comparator_3_eq, ocupada_via2);
  RAM #(.dataWidth(16), .bus("separate")) ram_7 (
    .addr(multiplexer_1_out), .din(register_2_q), .data(ram_7_data), .str(clk), .clk(and_11_out),
    .ld(L_E_ram), .clr(clear_ram));  // open: sel
  Register #(.width(13)) register_8 (.D(ram_6_data), .Q(register_8_q), .clk(clk));  // open: en, clr
  Multiplexer #(.enable("false")) multiplexer_9 (.in0(1'b0), .in1(and_12_out), .out(hit_via2), .sel(enable_salida_ram));
  Multiplexer #(.width(16), .enable("false")) multiplexer_10 (
    .in0({16{1'b0}}), .in1(register_9_q), .out(multiplexer_10_out), .sel(enable_salida_ram));
  Register #(.width(16)) register_9 (.D(ram_7_data), .Q(register_9_q), .clk(clk));  // open: en, clr
  not not_4 (not_4_out, ocupada_via0);
  not not_5 (not_5_out, ocupada_via1);
  not not_6 (not_6_out, ocupada_via2);
  not not_7 (not_7_out, ocupada_via3);
  not not_8 (not_8_out, ocupada_via4);
  and and_13 (and_13_out, w_via3, and_21_out);
  Comparator #(.width(13)) comparator_4 (.a(register_11_q), .b(address[20:8]), .eq(comparator_4_eq));  // open: gt, lt
  and and_14 (and_14_out, w_via3, and_19_out);
  RAM #(.dataWidth(13), .bus("separate")) ram_8 (
    .addr(multiplexer_1_out), .din(register_1_q), .data(ram_8_data), .str(clk), .clk(and_13_out),
    .ld(L_E_ram), .clr(clear_ram));  // open: sel
  and and_15 (and_15_out, comparator_4_eq, ocupada_via3);
  RAM #(.dataWidth(16), .bus("separate")) ram_9 (
    .addr(multiplexer_1_out), .din(register_2_q), .data(ram_9_data), .str(clk), .clk(and_14_out),
    .ld(L_E_ram), .clr(clear_ram));  // open: sel
  or or_1 (or_1_out, not_4_out, not_5_out, not_6_out, not_7_out, not_8_out);
  not not_9 (not_9_out, reset);
  Register #(.width(1)) register_10 (.D(valido), .Q(aun_vias_libres), .clk(clk));  // open: en, clr
  Register #(.width(13)) register_11 (.D(ram_8_data), .Q(register_11_q), .clk(clk));  // open: en, clr
  Multiplexer #(.enable("false")) multiplexer_11 (
    .in0(1'b0), .in1(and_15_out), .out(hit_via3), .sel(enable_salida_ram));
  Multiplexer #(.width(16), .enable("false")) multiplexer_12 (
    .in0({16{1'b0}}), .in1(register_12_q), .out(multiplexer_12_out), .sel(enable_salida_ram));
  Register #(.width(16)) register_12 (.D(ram_9_data), .Q(register_12_q), .clk(clk));  // open: en, clr
  and and_16 (valido, or_1_out, not_9_out);
  and and_17 (and_17_out, w_via4, and_21_out);
  Comparator #(.width(13)) comparator_5 (.a(register_14_q), .b(address[20:8]), .eq(comparator_5_eq));  // open: gt, lt
  and and_18 (and_18_out, and_19_out, w_via4);
  and and_19 (and_19_out, enable_w, clk);
  RAM #(.dataWidth(13), .bus("separate")) ram_10 (
    .addr(multiplexer_1_out), .din(register_1_q), .data(ram_10_data), .str(clk), .clk(and_17_out),
    .ld(L_E_ram), .clr(clear_ram));  // open: sel
  Multiplexer #(.enable("false")) multiplexer_13 (
    .in0(1'b0), .in1(and_20_out), .out(hit_via4), .sel(enable_salida_ram));
  and and_20 (and_20_out, comparator_5_eq, ocupada_via4);
  RAM #(.dataWidth(16), .bus("separate")) ram_11 (
    .addr(multiplexer_1_out), .din(register_2_q), .data(ram_11_data), .str(clk), .clk(and_18_out),
    .ld(L_E_ram), .clr(clear_ram));  // open: sel
  Register #(.width(16)) register_13 (.D(ram_11_data), .Q(register_13_q), .clk(clk));  // open: en, clr
  Register #(.width(13)) register_14 (.D(ram_10_data), .Q(register_14_q), .clk(clk));  // open: en, clr
  and and_21 (and_21_out, clk, enable_w);
  Multiplexer #(.width(16), .enable("false")) multiplexer_14 (
    .in0({16{1'b0}}), .in1(register_13_q), .out(multiplexer_14_out), .sel(enable_salida_ram));
  not not_10 (not_10_out, ocupada_via4);
  not not_11 (not_11_out, ocupada_via3);
  not not_12 (not_12_out, ocupada_via2);
  not not_13 (not_13_out, ocupada_via1);
  not not_14 (not_14_out, ocupada_via0);
  // Probe on via_a_escribir
  Priority_Encoder priority_encoder_2 (
    .in0(not_10_out), .in1(not_11_out), .in2(not_12_out), .in3(not_13_out), .in4(not_14_out),
    .out(via_a_escribir), .en_in(valido));  // open: in5, in6, in7, gs, en_out
  Decoder #(.select(3)) decoder_1 (
    .out0(w_via4), .out1(w_via3), .out2(w_via2), .out3(w_via1), .out4(w_via0), .sel(via_a_escribir),
    .en(enable_w_viaX));  // open: out5, out6, out7
  Register #(.width(3)) register_15 (.D(estado), .Q(register_15_q), .clk(clk));  // open: en, clr
  Register #(.width(3)) register_16 (.clk(clk));  // open: D, en, Q, clr
  // Probe on estado
  Register register_17 (.D(address[7:0]), .Q(register_17_q), .clk(or_2_out));  // open: en, clr
  or or_2 (or_2_out, clear_ram, enable_direccion);
  Register register_18 (.D(address[7:0]), .Q(register_18_q), .clk(or_2_out));  // open: en, clr
  Multiplexer #(.width(8), .enable("false")) multiplexer_15 (
    .in0(register_17_q), .in1(address[7:0]), .out(set_bueno), .sel(enable_direccion_valid));
  Multiplexer #(.width(8), .enable("false")) multiplexer_16 (
    .in0(register_18_q), .in1(address[7:0]), .out(set_bueno_valid), .sel(enable_direccion_valid));
  ROM #(.addrWidth(6), .dataWidth(3)) rom_1 (
    .addr({register_15_q, reset, request, L_E_prime}), .data(estado));  // open: sel
  ROM #(.addrWidth(6), .dataWidth(12)) rom_2 (
    .addr({register_15_q, reset, request, L_E_prime}),
    .data({error, enable_w_viaX, clear_ram, L_E_ram_valid, L_E_ram, enable_salida_ram, enable_direccion_valid, enable_direccion, enable_r_valid, enable_w_valid, enable_r, enable_w}));  // open: sel
  Register register_19 (.D(set_bueno), .Q(set_escribir), .clk(clk));  // open: en, clr
  Register register_20 (.D(set_bueno_valid), .Q(set_escribir_valid), .clk(clk));  // open: en, clr
  // Probe on address[20:8]
  // Probe on address[7:0]

  // Other names for the same wires on the sheet: Set[7:0] = address[7:0]; Tag[12:0] = address[20:8]

  // Notes on the sheet:
  //   Tags via 0
  //   Via 0
  //   Tags via 1
  //   Via 1
  //   Tags via 2
  //   Via 2
  //   Tags via 3
  //   Via 3
  //   Tags via 4
  //   Via 4
  //   contents of rom_1 (hex, n*v repeats v):
  //   1 6 2 1 4*0 4*1 4*0 6 6 3 1 4*0 6 6 2 4 4*0 6 6 1 5 4*0 6 6 1 4 4*0 6 6 2 4
  //   contents of rom_2 (hex, n*v repeats v):
  //   98a 18a 1aa 98a 4*200 4*98a 4*200 18a 18a 475 98a 4*200 18a 18a 1aa 1ba 4*200 98a 18a 98a 1fa 4*200
  //   98a 18a 98a 1ea 4*200 18a 18a 1aa 1ba 4*200
endmodule
