// Logisim project test2_cache.circ as structural Verilog: 1 circuit, main circuit main
module main (
);

  wire and_1_out, and_2_out, and_3_out, and_4_out, and_5_out, and_7_out, cada_2_ciclos, clk, comparator_1_eq,
       d_ff_1_q, d_ff_1_qn, d_ff_2_q, d_ff_3_q, d_ff_4_qn, enable, L_E_prime, main_1_error, main_1_valido,
       multiplexer_1_out, not_1_out, not_2_out, not_3_out, not_4_out, request, reset, reset_contadores;
  wire [2:0] counter_3_q;
  wire [7:0] counter_2_q, counter_4_q;
  wire [12:0] counter_5_q;
  wire [15:0] counter_6_q, main_1_salida, rom_2_data;
  wire [20:0] rom_3_data;

  Counter counter_1 (.clk(clk));  // open: load, D, count, Q, carry, clr
  D_Flip_Flop d_ff_1 (.clk(clk), .D(d_ff_1_qn), .Q(d_ff_1_q), .Qn(d_ff_1_qn));  // open: preset, en, reset
  and and_1 (and_1_out, clk, enable);
  Counter counter_2 (.Q(counter_2_q), .clk(d_ff_1_q));  // open: load, D, count, carry, clr
  Counter #(.width(3), .max('h7)) counter_3 (
    .Q(counter_3_q), .clk(and_1_out), .clr(and_5_out));  // open: load, D, count, carry
  Multiplexer #(.enable("false")) multiplexer_1 (.in0(and_3_out), .in1(1'b0), .out(multiplexer_1_out), .sel(not_1_out));
  not not_1 (not_1_out, comparator_1_eq);
  Comparator #(.width(3)) comparator_1 (.a(3'b111), .b(counter_3_q), .eq(comparator_1_eq));  // open: gt, lt
  Comparator #(.width(1)) comparator_2 (.a(counter_3_q[0]), .b(1'b0), .eq(cada_2_ciclos));  // open: gt, lt
  ROM #(.dataWidth(3)) rom_1 (.addr(counter_2_q), .data({reset, request, L_E_prime}));  // open: sel
  D_Flip_Flop d_ff_2 (.clk(clk), .D(multiplexer_1_out), .Q(d_ff_2_q), .en(comparator_1_eq));  // open: Qn, preset, reset
  not not_2 (not_2_out, d_ff_3_q);
  D_Flip_Flop d_ff_3 (.clk(clk), .D(comparator_1_eq), .Q(d_ff_3_q));  // open: Qn, preset, en, reset
  ROM #(.dataWidth(16)) rom_2 (.addr(counter_2_q), .data(rom_2_data));  // open: sel
  ROM #(.dataWidth(21)) rom_3 (.addr(counter_2_q), .data(rom_3_data));  // open: sel
  Counter counter_4 (.Q(counter_4_q), .clk(and_2_out), .clr(and_5_out));  // open: load, D, count, carry
  and and_2 (and_2_out, and_3_out, d_ff_2_q, clk);
  and and_3 (and_3_out, not_2_out, comparator_1_eq);
  Counter #(.width(13), .max('h1fff)) counter_5 (
    .Q(counter_5_q), .clk(and_4_out), .clr(and_5_out));  // open: load, D, count, carry
  and and_4 (and_4_out, cada_2_ciclos, clk);
  D_Flip_Flop d_ff_4 (.clk(clk), .D(reset_contadores), .Qn(d_ff_4_qn));  // open: Q, preset, en, reset
  and and_5 (and_5_out, reset_contadores, d_ff_4_qn);
  Clock clock_1 (.out(clk));
  // Probe on rom_3_data
  and and_6 (reset_contadores, request, L_E_prime);
  and and_7 (and_7_out, clk, cada_2_ciclos);
  cache_TFG_main main_1 (
    .activacion(rom_2_data), .address(rom_3_data), .L_E_prime(L_E_prime), .request(request), .reset(reset),
    .clk(clk), .valido(main_1_valido), .error(main_1_error), .salida(main_1_salida));
  Counter #(.width(16), .max('hffff)) counter_6 (.Q(counter_6_q), .clk(and_7_out));  // open: load, D, count, carry, clr
  // Probe on main_1_valido
  // Probe on main_1_salida
  // Probe on main_1_error
  not not_3 (not_3_out, L_E_prime);
  not not_4 (not_4_out, reset);
  and and_8 (enable, request, not_4_out);

  // Notes on the sheet:
  //   Activaciones
  //   ROM de acciones
  //   Address
  //   contents of rom_1 (hex, n*v repeats v):
  //   4 30*2 1 1 30*3 2 0 4 4 3 4 2 3
  //   contents of rom_2 (hex, n*v repeats v):
  //   0 0 1 2 3 4 5 6 7 8 9 a b c d e f 10 11 12 13 14 15 16 17 18 19 1a 1b 1c 1d 32*0 ffff 5*0 ffff
  //   contents of rom_3 (hex, n*v repeats v):
  //   0 0 100 200 300 400 501 601 701 801 901 a02 b02 c02 d02 e02 f03 1003 1103 1203 1303 1404 1504 1604
  //   1704 1804 1905 1a05 1b05 1c05 1d05 0 0 0 100 200 300 400 501 601 701 801 901 a02 b02 c02 d02 e02 f03
  //   1003 1103 1203 1303 1404 1504 1604 1704 1804 1905 1a05 1b05 1c05 1d05 1f06 0 0 0 100
  //   Aumento de set
  //   Aumento de TAG
endmodule
