// Logisim project test_cache.circ as structural Verilog: 1 circuit, main circuit main
module main (
);

  wire clk, main_1_error, main_1_valido;
  wire [2:0] rom_3_data;
  wire [3:0] counter_1_q, counter_2_q, counter_3_q;
  wire [15:0] main_1_salida, rom_1_data;
  wire [20:0] rom_2_data;

  Clock clock_1 (.out(clk));
  Counter #(.width(4), .max('hf)) counter_1 (.Q(counter_1_q), .clk(clk));  // open: load, D, count, carry, clr
  Counter #(.width(4), .max('hf)) counter_2 (.Q(counter_2_q), .clk(clk));  // open: load, D, count, carry, clr
  Counter #(.width(4), .max('hf)) counter_3 (.Q(counter_3_q), .clk(clk));  // open: load, D, count, carry, clr
  ROM #(.addrWidth(4), .dataWidth(16)) rom_1 (.addr(counter_1_q), .data(rom_1_data));  // open: sel
  ROM #(.addrWidth(4), .dataWidth(21)) rom_2 (.addr(counter_2_q), .data(rom_2_data));  // open: sel
  ROM #(.addrWidth(4), .dataWidth(3)) rom_3 (.addr(counter_3_q), .data(rom_3_data));  // open: sel
  // Probe on rom_2_data
  // Probe on rom_1_data
  cache_TFG_main main_1 (
    .activacion(rom_1_data), .address(rom_2_data), .L_E_prime(rom_3_data[0]), .request(rom_3_data[1]),
    .reset(rom_3_data[2]), .clk(clk), .valido(main_1_valido), .error(main_1_error), .salida(main_1_salida));
  // Probe on main_1_valido
  // Probe on main_1_error
  // Probe on main_1_salida

  // Notes on the sheet:
  //   contents of rom_1 (hex, n*v repeats v):
  //   0 0 cafe 0 beba 0 0 aaaa
  //   contents of rom_2 (hex, n*v repeats v):
  //   0 0 123ff 123ff 456ff 456ff 0 123aa 123aa 456ff
  //   contents of rom_3 (hex, n*v repeats v):
  //   4 4 4*2 0 2 2 3 1 2 4
  //   ROM de activaciones
  //   ROM de direcciones
endmodule
