// Logisim project test_cache_brams.circ as structural Verilog: 1 circuit, main circuit main
module main (
);

  wire clk, d_ff_1_q, d_ff_1_qn, L_E, main_1_error, main_1_valido, request, reset;
  wire [7:0] counter_1_q;
  wire [15:0] main_1_salida, rom_2_data;
  wire [20:0] rom_3_data;

  D_Flip_Flop d_ff_1 (.clk(clk), .D(d_ff_1_qn), .Q(d_ff_1_q), .Qn(d_ff_1_qn));  // open: preset, en, reset
  Counter counter_1 (.Q(counter_1_q), .clk(d_ff_1_q));  // open: load, D, count, carry, clr
  ROM #(.dataWidth(3)) rom_1 (.addr(counter_1_q), .data({reset, request, L_E}));  // open: sel
  ROM #(.dataWidth(16)) rom_2 (.addr(counter_1_q), .data(rom_2_data));  // open: sel
  ROM #(.dataWidth(21)) rom_3 (.addr(counter_1_q), .data(rom_3_data));  // open: sel
  // Probe on main_1_valido
  cache_brams_main main_1 (
    .activacion(rom_2_data), .address(rom_3_data), .L_E_prime(L_E), .request(request), .reset(reset),
    .clk(clk), .valido(main_1_valido), .error(main_1_error), .salida(main_1_salida));
  // Probe on main_1_salida
  Clock clock_1 (.out(clk));
  // Probe on main_1_error

  // Notes on the sheet:
  //   Entradas
  //   Activaciones
  //   Address
  //   contents of rom_1 (hex, n*v repeats v):
  //   4 30*2 1 1 30*3 2 0 4 4 3 4 2 3
  //   contents of rom_2 (hex, n*v repeats v):
  //   0 0 1 2 3 4 5 6 7 8 9 a b c d e f 10 11 12 13 14 15 16 17 18 19 1a 1b 1c 1d 32*0 ffff 5*0 ffff
  //   contents of rom_3 (hex, n*v repeats v):
  //   0 0 100 200 300 400 501 601 701 801 901 a02 b02 c02 d02 e02 f03 1003 1103 1203 1303 1404 1504 1604
  //   1704 1804 1905 1a05 1b05 1c05 1d05 0 0 0 100 200 300 400 501 601 701 801 901 a02 b02 c02 d02 e02 f03
  //   1003 1103 1203 1303 1404 1504 1604 1704 1804 1905 1a05 1b05 1c05 1d05 1f06 0 0 0 100
endmodule
